# Fritzing sketch busy-board (saved by Fritzing 0.9.3b)
breadboards: 1

parts:
  Part1 = Arduino Nano (Rev3.0)
  J1 = Power Jack [package=power_jack_pth]
  BUTTON1 = Arcade Button (green)
  BUTTON2 = Arcade Button (yellow)
  BUTTON3 = Arcade Button (red)
  BUTTON4 = Arcade Button (blue)
  BUTTON5 = Arcade Button (white)
  LED3 = LEDs [package=led10mm]
  LED6 = LEDs [package=led10mm]
  LED4 = LEDs [package=led10mm]
  LED2 = LEDs [package=led10mm]
  LED5 = LEDs [package=led10mm]

nets:
  GND: Part1.GND, J1.GND, BUTTON1.no_name_yet#1, BUTTON2.no_name_yet#1, BUTTON3.no_name_yet#1, BUTTON4.no_name_yet#1, BUTTON5.no_name_yet#1, LED3.A, LED6.A, LED4.A, LED2.A, LED5.A
  N1: Part1.D2, BUTTON1.no_name_yet#2
  N2: Part1.D3, LED2.C
  N3: Part1.D4, BUTTON2.no_name_yet#2
  N4: Part1.D5, LED4.C
  N5: Part1.D6, BUTTON3.no_name_yet#2
  N6: Part1.D7, LED5.C
  N7: Part1.D8, BUTTON4.no_name_yet#2
  N8: Part1.D9, LED6.C
  N9: Part1.D10, BUTTON5.no_name_yet#2
  N10: Part1.D11/MOSI, LED3.C
  N11: Part1.VIN, J1.PWR

custom parts:
  Arcade Button (green): Adafruit Arcade Button (green)
  Arcade Button (yellow): Adafruit Arcade Button (yellow)
  Arcade Button (red): Adafruit Arcade Button (red)
  Arcade Button (blue): Adafruit Arcade Button (blue)
  Arcade Button (white): Adafruit Arcade Button (white)
